# Fritzing sketch ESP32_Tracker (saved by Fritzing 0.9.3b)
circuit board: 8.7cm x 6cm
breadboards: 1

parts:
  PZ1 = Buzzer 12mm [package=buzzer-12mm]
  Part1 = Adafruit MicroSD card breakout board [part_number="Adafruit #254"]
  R1 = Resistor [tolerance=±5% resistance=220 package=THT]
  Q1 = NPN-Transistor [part_number=2N2222 package="TO92 [THT]"]
  U2 = Voltage Regulator - 5V [package="TO220 [THT]"]
  J1 = Camdenboss CTB0158-2 [part_number=CTB0158-2 package=THT]
  C1 = Electrolytic Capacitor [capacitance=10µF voltage=20V package="100 mil [THT, electrolytic]"]
  C2 = Electrolytic Capacitor [capacitance=10µF voltage=20V package="100 mil [THT, electrolytic]"]
  U1 = ESP32-38PinWide [part_number=ESP32-38PinWide]
  Part2 = u-blox NEO-6M GPS Breakout
  S1 = Round Pushbutton
  D1 = Rectifier Diode [part_number=1N4007 package="300 mil [THT]"]
  S2 = Round Pushbutton
  LED = LED - 3mm [color="Red (633nm)" package="3 mm [THT]"]
  R2 = Resistor [tolerance=±5% resistance=4.7k package=THT]

nets:
  N1: PZ1.1, U1.GPIO13
  GND: PZ1.2, Part1.GND, Q1.E, U2.GND, J1.pin1, C1.-, C2.-, U1.GND, S1.leg1, S2.leg0, LED.cathode
  VCC: Part1.VCC, U2.output_voltage, C1.+, U1.VIN, Part2.VCC
  N2: Part1.CLK, U1.GPIO18
  N3: Part1.DO, U1.GPIO19
  N4: Part1.DI, U1.GPIO23
  N5: Part1.CS, U1.GPIO5
  N6: Part1.CD, U1.GPIO15
  N7: R1.Pin_0, Q1.B
  N8: R1.Pin_1, U1.GPIO4
  N9: Q1.C, Part2.GND
  N10: U2.input_voltage, C2.+, D1.cathode
  N11: J1.pin2, D1.anode
  N12: U1.EN, S1.leg0
  N13: U1.GPIO2, R2.Pin_0
  N14: U1.GPIO0, S2.leg1
  N15: U1.GPIO16, Part2.TXD
  N16: U1.GPIO17, Part2.RXD
  N17: LED.anode, R2.Pin_1

notes:
  ESP32 Tracker v1.0 [CGB]

custom parts:
  Adafruit MicroSD card breakout board: Not just a simple breakout board, this microSD adapter goes the extra mile - designed for ease of use. Onboard 5v->3v regulator provides 150mA for power-hungry cards 3v level shifting means you can use this with ease on either 3v or 5v systems Uses a proper level shifting chip, not resistors: less problems, and faster read/write access Use 3 or 4 digital pins to read and write 2Gb+ of storage!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
  ESP32-38PinWide: Generic 38-Pin ESP32 with wide format (only access to one side of pins on a breadboard) based on Stephen Lilley's HiLetgo ESP-WROOM-32 ESP32 ESP-32S Development Board.
